// Logisim project Lab02Turan.circ as structural Verilog: 3 circuits, main circuit main
module main (
  input  A1,
  input  B1,
  input  C1,
  input  A2,
  input  B2,
  input  C2,
  input  D2,
  output True1,
  output True2
);

  Equation1 equation1_1 (.In1A(A1), .In1B(B1), .In1C(C1), .Out1(True1));
  Equation2 equation2_1 (.In2A(A2), .In2B(B2), .In2C(C2), .In2D(D2), .Ou2(True2));

  // Notes on the sheet:
  //   Turan Nurgozhin
  //   Lab 02: Boolean Equations
  //   March 06, 2024
endmodule

module Equation2 (
  input  In2A,
  input  In2B,
  input  In2C,
  input  In2D,
  output Ou2
);

  wire and_1_out, and_2_out, and_3_out, and_4_out;

  and and_1 (and_1_out, ~In2A, ~In2B, In2C, ~In2D);  // AND_Gate
  and and_2 (and_2_out, ~In2A, In2B, In2C, In2D);  // AND_Gate
  and and_3 (and_3_out, In2A, ~In2B, In2C, ~In2D);  // AND_Gate
  and and_4 (and_4_out, In2A, In2B, In2C, ~In2D);  // AND_Gate
  or or_1 (Ou2, and_1_out, and_2_out, and_3_out, and_4_out);

  // Notes on the sheet:
  //   (A'B'CD')+(A'BCD)+(AB'CD')+(ABCD')
endmodule

module Equation1 (
  input  In1A,
  input  In1B,
  input  In1C,
  output Out1
);

  wire and_1_out, and_2_out, and_3_out;

  and and_1 (and_1_out, ~In1A, In1B, ~In1C);  // AND_Gate
  and and_2 (and_2_out, In1A, ~In1B, ~In1C);  // AND_Gate
  and and_3 (and_3_out, In1A, In1B, In1C);
  or or_1 (Out1, and_1_out, and_2_out, and_3_out);

  // Notes on the sheet:
  //   (A'BC')+(AB'C')+(ABC)
endmodule
